# Fritzing sketch RFID Project-2 (saved by Fritzing 0.8.7b)
breadboards: 1

parts:
  Part1 = Arduino Mega ADK (Rev3)
  Part2 = RFID-RC522-v2
  Part3 = 4x4 Keypad [part_number=101207]

nets:
  N1: Part1.A0, Part3.1
  N2: Part1.A1, Part3.2
  N3: Part1.A2, Part3.3
  N4: Part1.A3, Part3.4
  N5: Part1.A4, Part3.5
  N6: Part1.A5, Part3.6
  N7: Part1.A6, Part3.7
  N8: Part1.A7, Part3.8
  GND: Part1.GND, Part2.GND
  N9: Part1.D9_PWM, Part2.SDA
  N10: Part1.D8_PWM, Part2.RST
  3V3: Part1.3V3, Part2.3.3V
  N11: Part1.D50/MISO, Part2.MISO
  N12: Part1.D51/MOSI, Part2.MOSI
  N13: Part1.D52/SCK, Part2.SCK

custom parts:
  RFID-RC522-v2: A simple China made RFID-RC522 Reader; do check the pin labels, as this is a MFRC522 based clone.
  4x4 Keypad: Matrix membrane keypad 4x4
